// Logisim project 8-bit.circ as structural Verilog: 1 circuit, main circuit main
module main (
  input  in_1,
  input  in_2,
  input  in_3,
  input  in_4,
  input  in_5,
  input  in_6,
  input  in_7,
  input  in_8,
  input  in_9,
  input  in_10,
  input  in_11,
  input  in_12,
  input  in_13,
  input  in_14,
  input  in_15,
  input  in_16,
  input  in_17,
  output out_18,
  output out_19,
  output out_20,
  output out_21,
  output out_22,
  output out_23,
  output out_24,
  output out_25
);

  wire and_1_out, and_2_out, and_3_out, and_4_out, and_5_out, and_6_out, and_7_out, and_8_out, and_9_out,
       and_10_out, and_11_out, and_12_out, and_13_out, and_14_out, and_15_out, and_16_out, and_17_out,
       or_1_out, or_2_out, or_3_out, or_4_out, or_5_out, or_6_out, or_7_out, or_8_out, xor_1_out, xor_2_out,
       xor_3_out, xor_4_out, xor_5_out, xor_6_out, xor_7_out, xor_8_out;

  xor xor_1 (xor_1_out, in_16, in_8);
  and and_1 (and_1_out, in_17, or_8_out);
  xor xor_2 (xor_2_out, in_15, in_7);
  xor xor_3 (xor_3_out, in_14, in_6);
  xor xor_4 (xor_4_out, in_13, in_5);
  xor xor_5 (xor_5_out, in_12, in_4);
  xor xor_6 (xor_6_out, in_11, in_3);
  xor xor_7 (xor_7_out, in_10, in_2);
  xor xor_8 (xor_8_out, in_9, in_1);
  xor xor_9 (out_25, xor_1_out, and_1_out);
  and and_2 (and_2_out, xor_1_out, and_1_out);
  and and_3 (and_3_out, in_16, in_8);
  xor xor_10 (out_24, xor_2_out, or_1_out);
  and and_4 (and_4_out, xor_2_out, or_1_out);
  and and_5 (and_5_out, in_15, in_7);
  xor xor_11 (out_23, xor_3_out, or_2_out);
  and and_6 (and_6_out, xor_3_out, or_2_out);
  and and_7 (and_7_out, in_14, in_6);
  xor xor_12 (out_22, xor_4_out, or_3_out);
  and and_8 (and_8_out, xor_4_out, or_3_out);
  and and_9 (and_9_out, in_13, in_5);
  xor xor_13 (out_21, xor_5_out, or_4_out);
  and and_10 (and_10_out, xor_5_out, or_4_out);
  and and_11 (and_11_out, in_12, in_4);
  xor xor_14 (out_20, xor_6_out, or_5_out);
  and and_12 (and_12_out, xor_6_out, or_5_out);
  and and_13 (and_13_out, in_11, in_3);
  xor xor_15 (out_19, xor_7_out, or_6_out);
  and and_14 (and_14_out, xor_7_out, or_6_out);
  and and_15 (and_15_out, in_10, in_2);
  xor xor_16 (out_18, xor_8_out, or_7_out);
  and and_16 (and_16_out, xor_8_out, or_7_out);
  and and_17 (and_17_out, in_9, in_1);
  or or_1 (or_1_out, and_2_out, and_3_out);
  or or_2 (or_2_out, and_4_out, and_5_out);
  or or_3 (or_3_out, and_6_out, and_7_out);
  or or_4 (or_4_out, and_8_out, and_9_out);
  or or_5 (or_5_out, and_10_out, and_11_out);
  or or_6 (or_6_out, and_12_out, and_13_out);
  or or_7 (or_7_out, and_14_out, and_15_out);
  or or_8 (or_8_out, and_16_out, and_17_out);
endmodule
